// Logisim project criptoULA.circ as structural Verilog: 6 circuits, main circuit main
module main (
  input  XOR,
  input  \César ,
  input  Criptografar___0___Decriptografar___1,
  input  [6:0] Chave_criptografica,
  output [6:0] out_5
);

  wire Clock, keyboard_1_avail, Reset_out;
  wire [2:0] uc_1_operacaoula;
  wire [6:0] charInput;

  Keyboard keyboard_1 (.clk(Clock), .re(1'b1), .clr(Reset_out), .avail(keyboard_1_avail), .data(charInput));
  Button Reset (.out(Reset_out));
  Clock clock_1 (.out(Clock));
  UC uc_1 (
    .\César (\César ), .CryptDecrypt(Criptografar___0___Decriptografar___1), .OperacaoULA(uc_1_operacaoula),
    .XOR(XOR));
  TTY tty_1 (.data(charInput), .clk(Clock), .we(keyboard_1_avail), .clr(Reset_out));
  ULA ula_1 (.A__caractere(charInput), .B__chave(Chave_criptografica), .\Operação (uc_1_operacaoula), .Output(out_5));
  TTY tty_2 (.data(out_5), .clk(Clock), .we(keyboard_1_avail), .clr(Reset_out));

  // Other names for the same wires on the sheet: cesar = \César ; charOutput[6:0] = out_5;
  //   chave[6:0] = Chave_criptografica; modo = Criptografar___0___Decriptografar___1

  // Notes on the sheet:
  //   ENTRADA
  //   Digite o texto
  //   SELEÇÃO DE CRIPTOGRAFIA
  //   Para aplicar XOR + César, selecione ambos ou nenhum tipo
  //   SELEÇAO DE MODO
  //   INPUT
  //   SAÍDA
  //   NÚCLEO CRIPTOGRÁFICO
  //   OUTPUT
endmodule

module ULA (
  input  [6:0] A__caractere,
  input  [6:0] B__chave,
  input  [2:0] \Operação ,
  output [6:0] Output
);

  wire [6:0] caesar_coder_1_output, caesar_coder_2_output, caesar_decoder_1_output, caesar_decoder_2_output,
       xor_1_out, xor_2_out, xor_3_out;

  assign xor_1_out = A__caractere ^ B__chave;  // XOR_Gate xor_1, 7 bits wide
  Caesar_coder caesar_coder_1 (
    .Caractere_ASCII_de_7_bits(A__caractere), .Deslocamento(B__chave), .Output(caesar_coder_1_output));
  Caesar_decoder caesar_decoder_1 (
    .Caractere_ASCII_de_7_bits(A__caractere), .Deslocamento(B__chave), .Output(caesar_decoder_1_output));
  Caesar_coder caesar_coder_2 (
    .Caractere_ASCII_de_7_bits(A__caractere), .Deslocamento(B__chave), .Output(caesar_coder_2_output));
  assign xor_2_out = A__caractere ^ B__chave;  // XOR_Gate xor_2, 7 bits wide
  assign xor_3_out = caesar_coder_2_output ^ B__chave;  // XOR_Gate xor_3, 7 bits wide
  Caesar_decoder caesar_decoder_2 (
    .Caractere_ASCII_de_7_bits(xor_2_out), .Deslocamento(B__chave), .Output(caesar_decoder_2_output));
  Multiplexer #(.select(3), .width(7), .enable("false")) multiplexer_1 (
    .in0(xor_1_out), .in1(caesar_coder_1_output), .in2(caesar_decoder_1_output), .in3(xor_3_out),
    .in4(caesar_decoder_2_output), .in5({7{1'b0}}), .in6({7{1'b0}}), .in7({7{1'b0}}), .out(Output),
    .sel(\Operação ));

  // Other names for the same wires on the sheet: A[6:0] = A__caractere; B[6:0] = B__chave; op[2:0] = \Operação 
endmodule

module Caesar_coder (
  input  [6:0] Caractere_ASCII_de_7_bits,
  input  [6:0] Deslocamento,
  output [6:0] Output
);

  wire \alphabet_tester_1_é_letra , \alphabet_tester_1_é_letra_minúscula , \alphabet_tester_2_é_letra ,
       \alphabet_tester_2_é_letra_minúscula , and_1_out, xnor_1_out;
  wire [6:0] adder_1_out, divider_1_rem, multiplexer_1_out, subtractor_1_out;

  Divider #(.width(7)) divider_1 (.a(Deslocamento), .b(7'b0011010), .rem(divider_1_rem));  // open: out, upper
  Adder #(.width(7)) adder_1 (.a(Caractere_ASCII_de_7_bits), .b(divider_1_rem), .out(adder_1_out));  // open: cin, cout
  Subtractor #(.width(7)) subtractor_1 (.a(adder_1_out), .b(7'b0011010), .out(subtractor_1_out));  // open: bin, bout
  Alphabet_tester alphabet_tester_1 (
    .Caractere_ASCII_de_7_bits(adder_1_out), .\É_letra (\alphabet_tester_1_é_letra ),
    .\É_letra_minúscula (\alphabet_tester_1_é_letra_minúscula ));  // open: É_letra_maiúscula
  Multiplexer #(.width(7), .enable("false")) multiplexer_1 (
    .in0(subtractor_1_out), .in1(adder_1_out), .out(multiplexer_1_out), .sel(and_1_out));
  and and_1 (and_1_out, \alphabet_tester_1_é_letra , xnor_1_out);
  xnor xnor_1 (xnor_1_out, \alphabet_tester_1_é_letra_minúscula , \alphabet_tester_2_é_letra_minúscula );
  Multiplexer #(.width(7), .enable("false")) multiplexer_2 (
    .in0(Caractere_ASCII_de_7_bits), .in1(multiplexer_1_out), .out(Output), .sel(\alphabet_tester_2_é_letra ));
  Alphabet_tester alphabet_tester_2 (
    .Caractere_ASCII_de_7_bits(Caractere_ASCII_de_7_bits), .\É_letra (\alphabet_tester_2_é_letra ),
    .\É_letra_minúscula (\alphabet_tester_2_é_letra_minúscula ));  // open: É_letra_maiúscula

  // Notes on the sheet:
  //   Soma o valor de deslocamento aos caracteres alfabéticos, mantendo-os nos ranges de upper case e lower case na tabela ASCII
endmodule

module Alphabet_tester (
  input  [6:0] Caractere_ASCII_de_7_bits,
  output \É_letra_maiúscula ,
  output \É_letra ,
  output \É_letra_minúscula 
);

  wire comparator_1_gt, comparator_2_lt, comparator_3_gt, comparator_4_lt;

  Comparator #(.width(7), .mode("unsigned")) comparator_1 (
    .a(Caractere_ASCII_de_7_bits), .b(7'b1000000), .gt(comparator_1_gt));  // open: eq, lt
  Comparator #(.width(7), .mode("unsigned")) comparator_2 (
    .a(Caractere_ASCII_de_7_bits), .b(7'b1011011), .lt(comparator_2_lt));  // open: gt, eq
  Comparator #(.width(7), .mode("unsigned")) comparator_3 (
    .a(Caractere_ASCII_de_7_bits), .b(7'b1100000), .gt(comparator_3_gt));  // open: eq, lt
  Comparator #(.width(7), .mode("unsigned")) comparator_4 (
    .a(Caractere_ASCII_de_7_bits), .b(7'b1111011), .lt(comparator_4_lt));  // open: gt, eq
  and and_1 (\É_letra_maiúscula , comparator_1_gt, comparator_2_lt);
  and and_2 (\É_letra_minúscula , comparator_3_gt, comparator_4_lt);
  or or_1 (\É_letra , \É_letra_maiúscula , \É_letra_minúscula );

  // Notes on the sheet:
  //   Verifica se um dado caractere ASCII é uma letra e se é maiúscula ou minúscula
endmodule

module Caesar_decoder (
  input  [6:0] Caractere_ASCII_de_7_bits,
  input  [6:0] Deslocamento,
  output [6:0] Output
);

  wire \alphabet_tester_1_é_letra , \alphabet_tester_1_é_letra_minúscula , \alphabet_tester_2_é_letra ,
       \alphabet_tester_2_é_letra_minúscula , and_1_out, xnor_1_out;
  wire [6:0] adder_1_out, divider_1_rem, multiplexer_1_out, subtractor_1_out;

  Divider #(.width(7)) divider_1 (.a(Deslocamento), .b(7'b0011010), .rem(divider_1_rem));  // open: out, upper
  Subtractor #(.width(7)) subtractor_1 (
    .a(Caractere_ASCII_de_7_bits), .b(divider_1_rem), .out(subtractor_1_out));  // open: bin, bout
  Adder #(.width(7)) adder_1 (.a(subtractor_1_out), .b(7'b0011010), .out(adder_1_out));  // open: cin, cout
  Alphabet_tester alphabet_tester_1 (
    .Caractere_ASCII_de_7_bits(subtractor_1_out), .\É_letra (\alphabet_tester_1_é_letra ),
    .\É_letra_minúscula (\alphabet_tester_1_é_letra_minúscula ));  // open: É_letra_maiúscula
  Multiplexer #(.width(7), .enable("false")) multiplexer_1 (
    .in0(adder_1_out), .in1(subtractor_1_out), .out(multiplexer_1_out), .sel(and_1_out));
  and and_1 (and_1_out, \alphabet_tester_1_é_letra , xnor_1_out);
  xnor xnor_1 (xnor_1_out, \alphabet_tester_1_é_letra_minúscula , \alphabet_tester_2_é_letra_minúscula );
  Multiplexer #(.width(7), .enable("false")) multiplexer_2 (
    .in0(Caractere_ASCII_de_7_bits), .in1(multiplexer_1_out), .out(Output), .sel(\alphabet_tester_2_é_letra ));
  Alphabet_tester alphabet_tester_2 (
    .Caractere_ASCII_de_7_bits(Caractere_ASCII_de_7_bits), .\É_letra (\alphabet_tester_2_é_letra ),
    .\É_letra_minúscula (\alphabet_tester_2_é_letra_minúscula ));  // open: É_letra_maiúscula

  // Notes on the sheet:
  //   Subtrai o valor de deslocamento dos caracteres alfabéticos, mantendo-os nos ranges de upper case e lower case na tabela ASCII
endmodule

module UC (
  input  CryptDecrypt,
  input  \César ,
  input  XOR,
  output [2:0] OperacaoULA
);

  wire and_2_out, and_3_out, and_4_out, or_2_out, xnor_1_out, xnor_2_out;

  xnor xnor_1 (xnor_1_out, XOR, \César );
  and and_1 (OperacaoULA[2], xnor_1_out, CryptDecrypt);
  xnor xnor_2 (xnor_2_out, XOR, \César );
  and and_2 (and_2_out, xnor_2_out, ~CryptDecrypt);  // AND_Gate
  and and_3 (and_3_out, ~XOR, \César , CryptDecrypt);  // AND_Gate
  or or_1 (OperacaoULA[1], and_2_out, and_3_out);
  and and_4 (and_4_out, XOR, \César );
  or or_2 (or_2_out, and_4_out, ~XOR);  // OR_Gate
  and and_5 (OperacaoULA[0], or_2_out, ~CryptDecrypt);  // AND_Gate

  // Notes on the sheet:
  //   Converte as opções nos bits de seleção da ULA correspondentes
endmodule
